# Fritzing sketch Line follower wiring schematic (saved by Fritzing 0.9.6b)
breadboards: 1

parts:
  M1 = gear-motor [part_number="MOTOR LEFT"]
  VCC1 = 4 x AAA Battery Mount
  HC-SR04_Sensor_1 = HC-SR04 Ultrasonic Distance Sensor
  U2 = QTR-3A Reflectance Sensor Array [package=THT]
  A1 = 1x18650 battery shield [package=THT]
  Part2 = Arduino Mega 2560 (Rev3)
  LCD2 = LCD screen
  LCM1602_IIC2 = LCM1602 IIC [part_number="LCM1602 IIC" chip_label="LCM1602 IIC" package="DIP (Dual Inline) [THT]"]
  U3 = L9110 H-bridge module [part_number="L9110 H-bridge"]
  S1 = Momentary Switch [package=ksa_sealed_tac_switch]
  R1 = Resistor [tolerance=±5% resistance=10k package="1206 [SMD]"]
  U4 = ESP32-38PinWide [part_number=ESP32-38PinWide]
  LED1 = RGB LED (com. anode, rbg) [package="5 mm [THT]"]
  R2 = Resistor [tolerance=±5% resistance=10k package="1206 [SMD]"]
  R3 = Resistor [tolerance=±5% resistance=10k package="1206 [SMD]"]
  R4 = Resistor [tolerance=±5% resistance=100 package="1206 [SMD]"]
  R5 = Resistor [tolerance=±5% resistance=100 package="1206 [SMD]"]
  R6 = Resistor [tolerance=±5% resistance=150 package="1206 [SMD]"]
  Mod1 = Passive Buzzer
  M2 = gear-motor [part_number="MOTOR RIGHT"]
  U5 = SWITCH-SPST-2 [package=r_sw_th]
  R7 = Resistor [tolerance=±5% resistance=10k package="2010 [SMD]"]  # not connected
  R8 = Resistor [tolerance=±5% resistance=20k package="2010 [SMD]"]

nets:
  N1: M1.pin_1, U3.MOTOR_B-B
  N2: M1.pin_2, U3.MOTOR_B-A
  N3: VCC1.+, U3.VCC
  VCC: HC-SR04_Sensor_1.VCC, A1.pin_7, Part2.5V, S1.3, R3.Pin_1
  N4: HC-SR04_Sensor_1.TRIG, Part2.D22
  N5: HC-SR04_Sensor_1.ECHO, Part2.D23
  N6: U2.GND, Part2.A2
  N7: U2.VCC, Part2.A1
  N8: U2.1, Part2.A0
  N9: Part2.A3, R2.Pin_0, R3.Pin_0
  N10: Part2.A4, LCM1602_IIC2.SDA
  N11: Part2.A5, LCM1602_IIC2.SCL
  N12: Part2.D13_PWM, S1.1, R1.Pin_1
  N13: Part2.D12_PWM, U4.GPIO17
  N14: Part2.D11_PWM, R8.Pin_0
  N15: Part2.D10_PWM, R4.Pin_1
  N16: Part2.D9_PWM, R5.Pin_1
  N17: Part2.D8_PWM, Mod1.S
  GND: Part2.GND, U3.GND, R1.Pin_0, LED1.common_anode, R2.Pin_1, Mod1.NC, Mod1.-
  N18: Part2.D3_PWM, U3.A-IB
  N19: Part2.D4_PWM, U3.A-IA
  N20: Part2.D5_PWM, R6.Pin_1
  N21: Part2.D6_PWM, U3.B-IB
  N22: Part2.D7_PWM, U3.B-IA
  VSS: LCD2.VSS, LCM1602_IIC2.VSS
  VDD: LCD2.VDD, LCM1602_IIC2.VDD
  N23: LCD2.V0, LCM1602_IIC2.V0
  N24: LCD2.RS, LCM1602_IIC2.RS
  N25: LCD2.R/W, LCM1602_IIC2.RW
  N26: LCD2.E, LCM1602_IIC2.E
  N27: LCD2.DB0, LCM1602_IIC2.D0
  N28: LCD2.DB1, LCM1602_IIC2.D1
  N29: LCD2.DB2, LCM1602_IIC2.D2
  N30: LCD2.DB3, LCM1602_IIC2.D3
  N31: LCD2.DB4, LCM1602_IIC2.D4
  N32: LCD2.DB5, LCM1602_IIC2.D5
  N33: LCD2.DB6, LCM1602_IIC2.D6
  N34: LCD2.DB7, LCM1602_IIC2.D7
  N35: LCD2.LED+, LCM1602_IIC2.A
  N36: LCD2.LED-, LCM1602_IIC2.K
  N37: LCM1602_IIC2.LED_A, LCM1602_IIC2.LED_B
  N38: U3.MOTOR_A-A, M2.pin_1
  N39: U3.MOTOR_A-B, M2.pin_2
  N40: U4.GPIO16, R8.Pin_1
  N41: LED1.red_cathode, R6.Pin_0
  N42: LED1.blue_cathode, R5.Pin_0
  N43: LED1.green_cathode, R4.Pin_0
  N44: U5.O, U5.P

custom parts:
  1x18650 battery shield: 1x18650 Lithium Battery Shield V3 CC CV Type-C Micro USB Mobile Power Bank DIY Module 5V 3A 3V 1A for iPhone Samsung Xiaomi.
  LCM1602 IIC: I2C-Module to use a 1602 or 2004 LCD on with the wire.h libory Serial LCD Modul
  ESP32-38PinWide: Generic 38-Pin ESP32 with wide format (only access to one side of pins on a breadboard) based on Stephen Lilley's HiLetgo ESP-WROOM-32 ESP32 ESP-32S Development Board.
